# Fritzing sketch ultrasonido (saved by Fritzing 0.9.3b)

parts:
  Part1 = Arduino Uno (Rev3)
  HC-SR04_Sensor_1 = HC-SR04 Ultrasonic Distance Sensor

nets:
  N1: Part1.D10_PWM/SS, HC-SR04_Sensor_1.TRIG
  N2: Part1.D11_PWM/MOSI, HC-SR04_Sensor_1.ECHO
  5V: Part1.5V, HC-SR04_Sensor_1.VCC
  GND: Part1.GND, HC-SR04_Sensor_1.GND

// code stored in the sketch: ultras.ino
const int trigger=10;
const int echo=11;

float time;
 int distancia;

void setup(){

pinMode(trigger,OUTPUT);
pinMode(echo,INPUT);
Serial.begin(9600);

}

void loop(){

digitalWrite(trigger,LOW);
delayMicroseconds(5);
digitalWrite(trigger,HIGH);
delayMicroseconds(10);

time=pulseIn(echo,HIGH);

distancia=(time/2)*(1/29.2);

Serial.print("Distancia: ")
Serial.print(distancia);
Serial.println(" cm");


}
